// Logisim project ch.circ as structural Verilog: 1 circuit, main circuit main
module main (
  input  in_1,
  input  in_2
);

  wire clock_1_out;
  wire [7:0] register_1_q_2;
  wire [23:0] register_1_q;
  wire [31:0] adder_1_out;

  Adder #(.width(32)) adder_1 (.a({register_1_q_2, register_1_q}), .b(32'h4), .out(adder_1_out));  // open: cin, cout
  Register #(.width(32)) register_1 (
    .D(adder_1_out), .en(in_1), .Q({register_1_q_2, register_1_q}), .clk(clock_1_out), .clr(in_2));
  Clock clock_1 (.out(clock_1_out));
  Adder #(.width(1)) adder_2 (.a(1'b1));  // open: b, out, cin, cout
  RAM #(.addrWidth(24), .dataWidth(32)) ram_1 (.addr(register_1_q), .clk(clock_1_out));  // open: data, sel, ld, clr
endmodule
